# Fritzing sketch esp8266_rst (saved by Fritzing 0.9.1b)
breadboards: 1

parts:
  Part1 = Arduino Leonardo (Rev3b)
  U1 = ESP8266 WiFi Module [part_number=ESP8266]

nets:
  N1: Part1.D0/RX, U1.TXD
  3V3: Part1.3V3, U1.VCC
  N2: Part1.D8/A8, U1.GPIO_16
  N3: Part1.D9_PWM/A9, U1.CH_PD

notes:
  VCC  RST   CH_PD VTXD
  VXRD GPIO0 GPIO2 GND

custom parts:
  ESP8266 WiFi Module: Generic WiFi Module based on the ESP8266 with onboard PCB antenna and UART communications
